// Logisim project ALUOp1.circ as structural Verilog
module ALUOp (
  input  [4:0] OP,
  input  [1:0] FUNC,
  output [2:0] ALUOp
);

  wire and_2_out, and_3_out, not_1_out;

  not not_1 (not_1_out, OP[3]);
  and and_1 (ALUOp[1], not_1_out, FUNC[1]);
  and and_2 (and_2_out, not_1_out, FUNC[0]);
  and and_3 (and_3_out, OP[2], OP[1]);
  or or_1 (ALUOp[0], and_2_out, and_3_out);

  assign ALUOp[2] = 1'b0;
endmodule
