// Logisim project Belal_Single_Cycle_CPU.circ as structural Verilog: 3 circuits, main circuit main
module main (
);

  wire clock_1_out, RegDst, splt_1_p4, WBdata, ZeroFlag;
  wire [1:0] PCSrc;
  wire [2:0] multiplexer_2_out, splt_1_p5, splt_1_p6;
  wire [4:0] splt_1_p3;
  wire [10:0] splt_1_p2;
  wire [15:0] adder_1_out, adder_2_out, alu_1_p2, bit_extender_1_out, bit_extender_2_out, multiplexer_1_out,
       multiplexer_3_out, ram_1_dout, register_1_q, registerfile_1_p5, registerfile_1_p6, rom_2_data;

  Multiplexer #(.select(2), .width(16)) multiplexer_1 (
    .in0(adder_1_out), .in1(bit_extender_1_out), .in2(adder_2_out), .out(multiplexer_1_out), .sel(PCSrc));  // open: in3
  Clock clock_1 (.out(clock_1_out));
  ROM #(.addrWidth(5), .dataWidth(5)) rom_1 ();  // open: addr, data
  ROM #(.addrWidth(16), .dataWidth(16)) rom_2 (.addr(register_1_q), .data(rom_2_data));
  Register #(.width(16)) register_1 (
    .D(multiplexer_1_out), .en(1'b1), .Q(register_1_q), .clk(clock_1_out));  // open: clr
  Adder #(.width(16)) adder_1 (.a(16'h1), .b(register_1_q), .out(adder_1_out));  // open: cin, cout
  Adder #(.width(16)) adder_2 (.a(register_1_q), .b(bit_extender_2_out), .out(adder_2_out));  // open: cin, cout
  // Splt splt_1: pin names not known; wires that end beside it: rom_2_data, splt_1_p2, splt_1_p3, splt_1_p4, splt_1_p5, splt_1_p6
  Multiplexer #(.width(3)) multiplexer_2 (.in0(splt_1_p5), .in1(splt_1_p6), .out(multiplexer_2_out), .sel(RegDst));
  assign bit_extender_1_out = {{5{1'b0}}, splt_1_p2};  // Bit_Extender bit_extender_1
  assign bit_extender_2_out = {{11{splt_1_p3[4]}}, splt_1_p3};  // Bit_Extender bit_extender_2
  // registerFile registerfile_1: pin names not known; wires that end beside it: splt_1_p4, splt_1_p5, multiplexer_2_out, ZeroFlag, registerfile_1_p5, registerfile_1_p6
  Multiplexer #(.width(16)) multiplexer_3 (
    .in0(registerfile_1_p6), .in1(bit_extender_2_out), .out(multiplexer_3_out));  // open: sel
  // ALU alu_1: pin names not known; wires that end beside it: multiplexer_3_out, alu_1_p2, alu_1_p2
  RAM #(.addrWidth(16), .dataWidth(16)) ram_1 (
    .addr(alu_1_p2), .clk(clock_1_out), .dout(ram_1_dout));  // open: we, oe, din
  Multiplexer #(.width(16)) multiplexer_4 (.in0(alu_1_p2), .in1(ram_1_dout), .out(registerfile_1_p5), .sel(WBdata));
endmodule

module registerFile (
  input  [2:0] RA,
  input  [2:0] RB,
  input  [15:0] BusW,
  input  [2:0] RW,
  input  RegW,
  output [15:0] BusB,
  output [15:0] BusA
);

  wire and_1_out, and_2_out, and_3_out, and_4_out, and_5_out, and_6_out, and_7_out, clock_1_out,
       decoder_1_out1, decoder_1_out2, decoder_1_out3, decoder_1_out4, decoder_1_out5, decoder_1_out6,
       decoder_1_out7, decoder_2_out0, decoder_2_out1, decoder_2_out2, decoder_2_out3, decoder_2_out4,
       decoder_2_out5, decoder_2_out6, decoder_2_out7, decoder_3_out0, decoder_3_out1, decoder_3_out2,
       decoder_3_out3, decoder_3_out4, decoder_3_out5, decoder_3_out6, decoder_3_out7;
  wire [15:0] register_1_q, register_2_q, register_3_q, register_4_q, register_5_q, register_6_q,
       register_7_q;

  Decoder #(.enable("false"), .select(3)) decoder_1 (
    .out1(decoder_1_out1), .out2(decoder_1_out2), .out3(decoder_1_out3), .out4(decoder_1_out4),
    .out5(decoder_1_out5), .out6(decoder_1_out6), .out7(decoder_1_out7), .sel(RW));  // open: out0
  and and_1 (and_1_out, decoder_1_out1, RegW);
  and and_2 (and_2_out, decoder_1_out2, RegW);
  and and_3 (and_3_out, decoder_1_out3, RegW);
  and and_4 (and_4_out, decoder_1_out4, RegW);
  and and_5 (and_5_out, decoder_1_out5, RegW);
  and and_6 (and_6_out, decoder_1_out6, RegW);
  and and_7 (and_7_out, decoder_1_out7, RegW);
  Decoder #(.enable("false"), .select(3)) decoder_2 (
    .out0(decoder_2_out0), .out1(decoder_2_out1), .out2(decoder_2_out2), .out3(decoder_2_out3),
    .out4(decoder_2_out4), .out5(decoder_2_out5), .out6(decoder_2_out6), .out7(decoder_2_out7), .sel(RA));
  Register #(.width(16)) register_1 (.D(BusW), .en(and_1_out), .Q(register_1_q), .clk(clock_1_out));  // open: clr
  Register #(.width(16)) register_2 (.D(BusW), .en(and_2_out), .Q(register_2_q), .clk(clock_1_out));  // open: clr
  Register #(.width(16)) register_3 (.D(BusW), .en(and_3_out), .Q(register_3_q), .clk(clock_1_out));  // open: clr
  Register #(.width(16)) register_4 (.D(BusW), .en(and_4_out), .Q(register_4_q), .clk(clock_1_out));  // open: clr
  Register #(.width(16)) register_5 (.D(BusW), .en(and_5_out), .Q(register_5_q), .clk(clock_1_out));  // open: clr
  Register #(.width(16)) register_6 (.D(BusW), .en(and_6_out), .Q(register_6_q), .clk(clock_1_out));  // open: clr
  Register #(.width(16)) register_7 (.D(BusW), .en(and_7_out), .Q(register_7_q), .clk(clock_1_out));  // open: clr
  Clock clock_1 (.out(clock_1_out));
  assign BusA = decoder_2_out0 ? {16{1'b0}} : 16'bz;  // Controlled_Buffer controlled_buffer_1
  assign BusA = decoder_2_out1 ? register_1_q : 16'bz;  // Controlled_Buffer controlled_buffer_2
  assign BusA = decoder_2_out2 ? register_2_q : 16'bz;  // Controlled_Buffer controlled_buffer_3
  assign BusA = decoder_2_out3 ? register_3_q : 16'bz;  // Controlled_Buffer controlled_buffer_4
  assign BusA = decoder_2_out4 ? register_4_q : 16'bz;  // Controlled_Buffer controlled_buffer_5
  assign BusA = decoder_2_out5 ? register_5_q : 16'bz;  // Controlled_Buffer controlled_buffer_6
  assign BusA = decoder_2_out6 ? register_6_q : 16'bz;  // Controlled_Buffer controlled_buffer_7
  assign BusA = decoder_2_out7 ? register_7_q : 16'bz;  // Controlled_Buffer controlled_buffer_8
  Decoder #(.enable("false"), .select(3)) decoder_3 (
    .out0(decoder_3_out0), .out1(decoder_3_out1), .out2(decoder_3_out2), .out3(decoder_3_out3),
    .out4(decoder_3_out4), .out5(decoder_3_out5), .out6(decoder_3_out6), .out7(decoder_3_out7), .sel(RB));
  assign BusB = decoder_3_out1 ? register_1_q : 16'bz;  // Controlled_Buffer controlled_buffer_9
  assign BusB = decoder_3_out2 ? register_2_q : 16'bz;  // Controlled_Buffer controlled_buffer_10
  assign BusB = decoder_3_out3 ? register_3_q : 16'bz;  // Controlled_Buffer controlled_buffer_11
  assign BusB = decoder_3_out4 ? register_4_q : 16'bz;  // Controlled_Buffer controlled_buffer_12
  assign BusB = decoder_3_out5 ? register_5_q : 16'bz;  // Controlled_Buffer controlled_buffer_13
  assign BusB = decoder_3_out6 ? register_6_q : 16'bz;  // Controlled_Buffer controlled_buffer_14
  assign BusB = decoder_3_out7 ? register_7_q : 16'bz;  // Controlled_Buffer controlled_buffer_15
  assign BusB = decoder_3_out0 ? {16{1'b0}} : 16'bz;  // Controlled_Buffer controlled_buffer_16
endmodule

module CU (
  input  [4:0] OP,
  output RegDst,
  output RegWrite,
  output EXTOp,
  output ALUSrc,
  output MemRead,
  output MemWrite,
  output WBData,
  output JAL,
  output LUI
);

  wire and_1_out, and_2_out, and_3_out, and_4_out, and_5_out, and_6_out, not_1_out, not_3_out, not_4_out,
       not_5_out;

  not not_1 (not_1_out, OP[4]);
  not not_2 (RegDst, OP[3]);
  not not_3 (not_3_out, OP[2]);
  not not_4 (not_4_out, OP[1]);
  not not_5 (not_5_out, OP[0]);
  and and_1 (and_1_out, not_1_out, not_3_out);
  and and_2 (and_2_out, not_1_out, not_4_out, not_5_out);
  and and_3 (and_3_out, OP[4], OP[0]);
  and and_4 (and_4_out, not_4_out, not_5_out);
  and and_5 (and_5_out, OP[3], not_3_out);
  and and_6 (and_6_out, OP[2], not_4_out);
  and and_7 (MemRead, OP[2], not_4_out, not_5_out);
  and and_8 (MemWrite, OP[2], not_4_out, OP[0]);
  and and_9 (WBData, OP[2], not_4_out);
  and and_10 (JAL, OP[4], RegDst, OP[0]);
  and and_11 (LUI, OP[4], OP[1]);
  or or_1 (RegWrite, and_1_out, and_2_out, and_3_out);
  or or_2 (EXTOp, and_4_out, OP[2]);
  or or_3 (ALUSrc, and_5_out, and_6_out);
endmodule
